# Fritzing sketch board (saved by Fritzing 0.9.3b)
breadboards: 3

parts:
  Part1 = Arduino Uno (Rev3)
  Part3 = RFID-RC522-v2  # not connected
  R1 = Resistor [tolerance=±5% resistance=220 package=THT]
  R2 = Trimmer Potentiometer [maximum_resistance=10kΩ package=THT]
  LED1 = LED - 5mm [color="Blue (470nm)" package="5 mm [THT]"]
  U1 = 74HC595 [package="DIP16 [THT]"]  # not connected
  J1 = Basic Servo  # not connected
  LCD1 = LCD screen
  R3 = Resistor [tolerance=±5% resistance=220 package=THT]
  R4 = Resistor [tolerance=±5% resistance=220 package=THT]
  R5 = Resistor [tolerance=±5% resistance=220 package=THT]
  R6 = Resistor [tolerance=±5% resistance=220 package=THT]
  R7 = Resistor [tolerance=±5% resistance=220 package=THT]
  R8 = Resistor [tolerance=±5% resistance=220 package=THT]
  R9 = Resistor [tolerance=±5% resistance=220 package=THT]
  LED2 = LED - 5mm [color="Blue (470nm)" package="5 mm [THT]"]
  LED3 = LED - 5mm [color="Green (555nm)" package="5 mm [THT]"]
  LED4 = LED - 5mm [color="Green (555nm)" package="5 mm [THT]"]
  LED5 = LED - 5mm [color="Red (633nm)" package="5 mm [THT]"]
  LED6 = LED - 5mm [color="Red (633nm)" package="5 mm [THT]"]
  LED7 = LED - 5mm [color="Yellow (585nm)" package="5 mm [THT]"]
  LED8 = LED - 5mm [color="Yellow (585nm)" package="5 mm [THT]"]

nets:
  N1: Part1.D8, LCD1.DB7
  N2: Part1.D3_PWM, LCD1.RS
  N3: Part1.D4, LCD1.E
  N4: Part1.D5_PWM, LCD1.DB4
  N5: Part1.D6_PWM, LCD1.DB5
  N6: Part1.D7, LCD1.DB6
  5V: Part1.5V, R2.leg1, LCD1.VDD, LCD1.LED+
  GND: Part1.GND, R2.leg2, LCD1.VSS, LCD1.R/W, LCD1.LED-
  N7: R1.Pin_1, LED3.anode
  N8: R2.wiper, LCD1.V0
  N9: LED1.cathode, LED2.cathode, LED3.cathode, LED4.cathode, LED5.cathode, LED6.cathode, LED7.cathode, LED8.cathode
  N10: LED1.anode, R5.Pin_1
  N11: R3.Pin_1, LED8.anode
  N12: R4.Pin_1, LED4.anode
  N13: R6.Pin_1, LED2.anode
  N14: R7.Pin_1, LED5.anode
  N15: R8.Pin_1, LED6.anode
  N16: R9.Pin_1, LED7.anode

custom parts:
  RFID-RC522-v2: A simple China made RFID-RC522 Reader; do check the pin labels, as this is a MFRC522 based clone.
